# Fritzing sketch Flex Sensor (saved by Fritzing 0.9.2b)
breadboards: 1

parts:
  Part1 = Arduino Uno (Rev3) - ICSP
  R2 = Resistor [tolerance=±5% resistance=220 package=THT]
  R3 = Basic Flex Resistor

nets:
  N1: Part1.A0, R2.Pin_1, R3.pin_1
  N2: Part1.5V, R3.Pin_2
  N3: Part1.GND, R2.Pin_0
